// Logisim project cpu.circ as structural Verilog: 13 circuits, main circuit main
module main (
);

  wire clock_1_out, counter_1_carry, cpu_1_loadmemory, not_1_out;
  wire [3:0] cpu_1_out_6, demultiplexer_1_out1, ram_1_data;
  wire [5:0] cpu_1_address;
  wire [7:0] counter_1_q;
  wire [9:0] rom_1_data;

  Counter counter_1 (.Q(counter_1_q), .carry(counter_1_carry), .clk(clock_1_out));  // open: load, D, count, clr
  RAM #(.addrWidth(6), .dataWidth(4)) ram_1 (
    .addr(cpu_1_address), .data(ram_1_data), .sel(1'b1), .clk(not_1_out), .ld(cpu_1_loadmemory));  // open: clr
  ROM #(.dataWidth(10)) rom_1 (.addr(counter_1_q), .data(rom_1_data), .sel(1'b1));
  not not_1 (not_1_out, clock_1_out);
  Clock clock_1 (.out(clock_1_out));
  Demultiplexer #(.width(4), .enable("false")) demultiplexer_1 (
    .out1(demultiplexer_1_out1), .in(ram_1_data), .sel(cpu_1_loadmemory));  // open: out0
  Multiplexer #(.width(4), .enable("false")) multiplexer_1 (
    .in0(cpu_1_out_6), .out(ram_1_data), .sel(cpu_1_loadmemory));  // open: in1
  CPU cpu_1 (
    .RAMData(demultiplexer_1_out1), .C(clock_1_out), .in_3(rom_1_data), .Address(cpu_1_address),
    .LoadMemory(cpu_1_loadmemory), .out_6(cpu_1_out_6));
  Hex_Digit_Display hex_digit_display_1 (.value(cpu_1_out_6), .dp(counter_1_carry));

  // Notes on the sheet:
  //   contents of rom_1 (hex, n*v repeats v):
  //   0 0 1c 1d 10 30 31 32 0 302 0 0 203 1f0 304
endmodule

module And (
  input  [3:0] A,
  input  [3:0] B,
  output [3:0] S
);

  and and_1 (S[0], A[0], B[0]);
  and and_2 (S[1], A[1], B[1]);
  and and_3 (S[2], A[2], B[2]);
  and and_4 (S[3], A[3], B[3]);
endmodule

module Or (
  input  [3:0] A,
  input  [3:0] B,
  output [3:0] S
);

  or or_1 (S[0], A[0], B[0]);
  or or_2 (S[1], A[1], B[1]);
  or or_3 (S[2], A[2], B[2]);
  or or_4 (S[3], A[3], B[3]);
endmodule

module Xor (
  input  [3:0] A,
  input  [3:0] B,
  output [3:0] S
);

  xor xor_1 (S[0], A[0], B[0]);
  xor xor_2 (S[1], A[1], B[1]);
  xor xor_3 (S[2], A[2], B[2]);
  xor xor_4 (S[3], A[3], B[3]);
endmodule

module Adder1 (
  input  A,
  input  B,
  output S,
  output C
);

  xor xor_1 (S, A, B);
  and and_1 (C, A, B);
endmodule

module Adder1C (
  input  A,
  input  B,
  input  C,
  output S,
  output C_2
);

  wire adder1_1_c, adder1_1_s, adder1_2_c;

  Adder1 adder1_1 (.A(A), .B(B), .S(adder1_1_s), .C(adder1_1_c));
  Adder1 adder1_2 (.A(adder1_1_s), .B(C), .S(S), .C(adder1_2_c));
  or or_1 (C_2, adder1_1_c, adder1_2_c);
endmodule

module Adder (
  input  [3:0] A,
  input  [3:0] B,
  output [3:0] S,
  output C
);

  wire adder1_1_c, adder1c_1_c_2, adder1c_2_c_2;

  Adder1 adder1_1 (.A(A[0]), .B(B[0]), .S(S[0]), .C(adder1_1_c));
  Adder1C adder1c_1 (.A(adder1_1_c), .B(A[1]), .C(B[1]), .S(S[1]), .C_2(adder1c_1_c_2));
  Adder1C adder1c_2 (.A(adder1c_1_c_2), .B(A[2]), .C(B[2]), .S(S[2]), .C_2(adder1c_2_c_2));
  Adder1C adder1c_3 (.A(adder1c_2_c_2), .B(A[3]), .C(B[3]), .S(S[3]), .C_2(C));
endmodule

module Transmission (
  input  O,
  input  [3:0] A,
  input  [3:0] B,
  output [3:0] Sa,
  output [3:0] Sb
);

  wire not_1_out;

  not not_1 (not_1_out, O);
  // Transmission_Gate #(.width(4)) transmission_1: pin names not known; wires that end beside it: A, O, not_1_out, O, Sa
  // Transmission_Gate #(.width(4)) transmission_2: pin names not known; wires that end beside it: B, not_1_out, O, Sb
endmodule

module ALU (
  input  [3:0] A,
  input  [3:0] B,
  input  [2:0] O,
  output [3:0] S,
  output CF
);

  wire [3:0] adder_1_s, and_1_s, or_1_s, xor_1_s;

  And and_1 (.A(A), .B(B), .S(and_1_s));
  Or or_1 (.A(A), .B(B), .S(or_1_s));
  Xor xor_1 (.A(A), .B(B), .S(xor_1_s));
  Adder adder_1 (.A(A), .B(B), .S(adder_1_s), .C(CF));
  Multiplexer #(.select(3), .width(4)) multiplexer_1 (
    .in1(and_1_s), .in2(or_1_s), .in3(xor_1_s), .in4(adder_1_s), .in7(4'b0001), .out(S), .sel(O), .en(1'b1));  // open: in0, in5, in6
endmodule

module Register (
  input  [3:0] I,
  input  C,
  output [3:0] O
);

  D_Flip_Flop d_ff_1 (.clk(C), .D(I[0]), .Q(O[0]));  // open: Qn, preset, en, reset
  D_Flip_Flop d_ff_2 (.clk(C), .D(I[1]), .Q(O[1]));  // open: Qn, preset, en, reset
  D_Flip_Flop d_ff_3 (.clk(C), .D(I[2]), .Q(O[2]));  // open: Qn, preset, en, reset
  D_Flip_Flop d_ff_4 (.clk(C), .D(I[3]), .Q(O[3]));  // open: Qn, preset, en, reset
endmodule

module RegisterBank (
  input  [3:0] I,
  input  [1:0] O,
  input  C,
  output [3:0] A,
  output [3:0] B,
  output [3:0] C_2,
  output [3:0] D
);

  wire demultiplexer_2_out0, demultiplexer_2_out1, demultiplexer_2_out2, demultiplexer_2_out3, not_1_out;
  wire [3:0] demultiplexer_1_out0, demultiplexer_1_out1, demultiplexer_1_out2, demultiplexer_1_out3;

  Demultiplexer #(.select(2), .width(4)) demultiplexer_1 (
    .out0(demultiplexer_1_out0), .out1(demultiplexer_1_out1), .out2(demultiplexer_1_out2),
    .out3(demultiplexer_1_out3), .in(I), .sel(O), .en(1'b1));
  Register register_1 (.C(demultiplexer_2_out0), .I(demultiplexer_1_out0), .O(A));
  Register register_2 (.C(demultiplexer_2_out1), .I(demultiplexer_1_out1), .O(B));
  Demultiplexer #(.select(2)) demultiplexer_2 (
    .out0(demultiplexer_2_out0), .out1(demultiplexer_2_out1), .out2(demultiplexer_2_out2),
    .out3(demultiplexer_2_out3), .in(not_1_out), .sel(O), .en(1'b1));
  not not_1 (not_1_out, C);
  Register register_3 (.C(demultiplexer_2_out2), .I(demultiplexer_1_out2), .O(C_2));
  Register register_4 (.C(demultiplexer_2_out3), .I(demultiplexer_1_out3), .O(D));
endmodule

module CPU (
  input  C,
  input  [3:0] RAMData,
  input  [9:0] in_3,
  output [5:0] Address,
  output LoadMemory,
  output [3:0] out_6
);

  wire not_1_out, not_2_out;
  wire [1:0] demultiplexer_1_out0_2, demultiplexer_1_out0_3, memorymanager_1_rread, memorymanager_1_rwrite,
       multiplexer_2_out, multiplexer_4_out;
  wire [3:0] alu_1_s, memorymanager_1_dataoutput, multiplexer_1_out, multiplexer_3_out, multiplexer_5_out,
       registerbank_1_a, registerbank_1_b, registerbank_1_c_2, registerbank_1_d;
  wire [4:0] demultiplexer_1_out0;
  wire [8:0] demultiplexer_1_out1;

  RegisterBank registerbank_1 (
    .I(out_6), .O(multiplexer_4_out), .C(C), .A(registerbank_1_a), .B(registerbank_1_b),
    .C_2(registerbank_1_c_2), .D(registerbank_1_d));
  not not_1 (not_1_out, LoadMemory);
  Multiplexer #(.select(2), .width(4), .enable("false")) multiplexer_1 (
    .in0(registerbank_1_a), .in1(registerbank_1_b), .in2(registerbank_1_c_2), .in3(registerbank_1_d),
    .out(multiplexer_1_out), .sel(multiplexer_2_out));
  Multiplexer #(.width(2), .enable("false")) multiplexer_2 (
    .in0(demultiplexer_1_out0_3), .in1(memorymanager_1_rread), .out(multiplexer_2_out), .sel(not_1_out));
  Multiplexer #(.select(2), .width(4), .enable("false")) multiplexer_3 (
    .in0(registerbank_1_a), .in1(registerbank_1_b), .in2(registerbank_1_c_2), .in3(registerbank_1_d),
    .out(multiplexer_3_out), .sel(demultiplexer_1_out0_2));
  Multiplexer #(.width(2), .enable("false")) multiplexer_4 (
    .in0(memorymanager_1_rwrite), .in1(demultiplexer_1_out0[1:0]), .out(multiplexer_4_out), .sel(not_2_out));
  Demultiplexer #(.width(9), .enable("false")) demultiplexer_1 (
    .out0({demultiplexer_1_out0_3, demultiplexer_1_out0_2, demultiplexer_1_out0}),
    .out1(demultiplexer_1_out1), .in(in_3[8:0]), .sel(in_3[9]));
  Hex_Digit_Display hex_digit_display_1 (.value(multiplexer_1_out));  // open: dp
  not not_2 (not_2_out, in_3[9]);
  Hex_Digit_Display hex_digit_display_2 (.value(multiplexer_3_out));  // open: dp
  Multiplexer #(.width(4), .enable("false")) multiplexer_5 (
    .in0(multiplexer_1_out), .in1(RAMData), .out(multiplexer_5_out), .sel(LoadMemory));
  MemoryManager memorymanager_1 (
    .DataInput(multiplexer_5_out), .in_2(demultiplexer_1_out1), .DataOutput(memorymanager_1_dataoutput),
    .Rread(memorymanager_1_rread), .Rwrite(memorymanager_1_rwrite), .Address(Address), .RAMread(LoadMemory));
  ALU alu_1 (.A(multiplexer_1_out), .B(multiplexer_3_out), .O(demultiplexer_1_out0[4:2]), .S(alu_1_s));  // open: CF
  Hex_Digit_Display hex_digit_display_3 (.value(alu_1_s));  // open: dp
  Multiplexer #(.width(4), .enable("false")) multiplexer_6 (
    .in0(alu_1_s), .in1(memorymanager_1_dataoutput), .out(out_6), .sel(in_3[9]));
endmodule

module MemoryManager (
  input  [3:0] DataInput,
  input  [8:0] in_2,
  output [3:0] DataOutput,
  output [1:0] Rread,
  output [1:0] Rwrite,
  output [5:0] Address,
  output RAMread
);

  not not_1 (RAMread, in_2[8]);
  Demultiplexer #(.width(2), .enable("false")) demultiplexer_1 (
    .out0(Rread), .out1(Rwrite), .in(in_2[1:0]), .sel(RAMread));

  assign Address = in_2[7:2];
  assign DataOutput = DataInput;
endmodule
